# Fritzing sketch fritzing (saved by Fritzing 0.9.3b)

parts:
  R1 = Rotary Potentiometer (Small) [maximum_resistance=100kΩ package=THT]
  Componente1 = Arduino Uno (Rev3)

nets:
  N1: R1.leg1, Componente1.GND
  N2: R1.wiper, Componente1.A2
  N3: R1.leg2, Componente1.5V
